// Logisim project Lab 2.circ as structural Verilog: 10 circuits, main circuit Main
module Main (
);

  wire ALUSrc, Branch, Clock, comparator_3_eq, comparator_4_eq, Jal, Jr, Jump, MemRead, MemWr, out, PCSrc,
       WrReg, Zero;
  wire [1:0] MemtoReg, RegDst;
  wire [2:0] ALUOp;
  wire [3:0] ALUCtl;
  wire [4:0] WrAddr;
  wire [5:0] func;
  wire [15:6] R_Type_Instruction;
  wire [25:0] shifter_2_out;
  wire [31:0] adder_1_out, adder_2_out, ALUResult, forJR, MemData, multiplexer_2_out, multiplexer_3_out,
       multiplexer_4_out, multiplexer_6_out, PC, PC_4, register_file_1_rddata2, shifter_1_out, Sign_Extend,
       toPC;
  wire [31:16] I_Type_Instruction;

  Clock clock_1 (.out(Clock));
  Multiplexer #(.select(2), .width(5), .enable("false")) multiplexer_1 (
    .in0(R_Type_Instruction[15:11]), .in1(I_Type_Instruction[20:16]), .in2({5{1'b1}}), .out(WrAddr),
    .sel({Jal, out}));  // open: in3
  Register_File register_file_1 (
    .WrAddr(WrAddr), .WrData(multiplexer_6_out), .WrReg(WrReg), .RdAddr1(I_Type_Instruction[25:21]),
    .RdAddr2(I_Type_Instruction[20:16]), .RdData1(forJR), .RdData2(register_file_1_rddata2), .Clock(Clock));
  Adder #(.width(32)) adder_1 (.a(PC), .b(32'h4), .out(adder_1_out));  // open: cin, cout
  Shifter #(.width(32)) shifter_1 (.in(Sign_Extend), .\dist (5'b00010), .out(shifter_1_out));
  ROM #(.dataWidth(32)) rom_1 (.addr(PC[9:2]), .data({I_Type_Instruction, R_Type_Instruction, func}));  // open: sel
  Adder #(.width(32)) adder_2 (.a(adder_1_out), .b(shifter_1_out), .out(adder_2_out));  // open: cin, cout
  Multiplexer #(.width(32), .enable("false")) multiplexer_2 (
    .in0(register_file_1_rddata2), .in1(Sign_Extend), .out(multiplexer_2_out), .sel(ALUSrc));
  Multiplexer #(.width(32), .enable("false")) multiplexer_3 (
    .in0(adder_1_out), .in1(adder_2_out), .out(multiplexer_3_out), .sel(PCSrc));
  and and_1 (PCSrc, Branch, Zero);
  ALU alu_1 (
    .ALUCtl(ALUCtl), .A(forJR), .B(multiplexer_2_out), .ALUResult(ALUResult), .Zero(Zero));  // open: Overflow, Shamt
  Shifter #(.width(26)) shifter_2 (
    .in({I_Type_Instruction[25:16], R_Type_Instruction, func}), .\dist (5'b00010), .out(shifter_2_out));
  Register #(.width(32)) register_1 (.D(toPC), .Q(PC), .clk(Clock));  // open: en, clr
  or or_1 (out, ALUSrc, MemRead);
  Multiplexer #(.width(32), .enable("false")) multiplexer_4 (
    .in0(multiplexer_3_out), .in1({adder_1_out[31:28], shifter_2_out, 2'b00}), .out(multiplexer_4_out),
    .sel(Jump));
  Multiplexer #(.width(32), .enable("false")) multiplexer_5 (
    .in0(multiplexer_4_out), .in1(forJR), .out(toPC), .sel(Jr));
  Adder #(.width(32)) adder_3 (.a(PC), .b(32'h4), .out(PC_4));  // open: cin, cout
  assign Sign_Extend = {{16{1'b0}}, {R_Type_Instruction, func}};  // Bit_Extender bit_extender_1
  JalMainControl jalmaincontrol_1 (
    .op5(I_Type_Instruction[31]), .op4(I_Type_Instruction[30]), .op3(I_Type_Instruction[29]),
    .op2(I_Type_Instruction[28]), .op1(I_Type_Instruction[27]), .op0(I_Type_Instruction[26]),
    .RegDst(RegDst[1]), .RegDst0(RegDst[0]), .ALUSrc(ALUSrc), .MemToReg(MemtoReg[1]),
    .MemToReg0(MemtoReg[0]), .RegWrite(WrReg), .MemRead(MemRead), .MemWrite(MemWr), .Branch(Branch),
    .ALUOp2(ALUOp[2]), .ALUOp1(ALUOp[1]), .ALUOp0(ALUOp[0]));
  RAM #(.dataWidth(32), .bus("separate")) ram_1 (
    .addr(ALUResult[7:0]), .din(register_file_1_rddata2), .data(MemData), .str(MemWr), .clk(Clock),
    .ld(MemRead));  // open: sel, clr
  Multiplexer #(.select(2), .width(32), .enable("false")) multiplexer_6 (
    .in0(ALUResult), .in1(MemData), .in2(PC_4), .out(multiplexer_6_out), .sel(MemtoReg));  // open: in3
  Comparator #(.width(6)) comparator_1 (.a(I_Type_Instruction[31:26]), .b(6'b000010), .eq(Jump));  // open: gt, lt
  Comparator #(.width(6)) comparator_2 (.a(I_Type_Instruction[31:26]), .b(6'b000011), .eq(Jal));  // open: gt, lt
  Comparator #(.width(6)) comparator_3 (.a(func), .b(6'b001000), .eq(comparator_3_eq));  // open: gt, lt
  Comparator #(.width(6)) comparator_4 (
    .a(I_Type_Instruction[31:26]), .b({6{1'b0}}), .eq(comparator_4_eq));  // open: gt, lt
  ALU_CONTROL alu_control_1 (
    .ALUOp2(ALUOp[2]), .ALUOp1(ALUOp[1]), .ALUOp0(ALUOp[0]), .func5(func[5]), .func4(func[4]),
    .func3(func[3]), .func2(func[2]), .func1(func[1]), .func0(func[0]), .ALUCtl3(ALUCtl[3]),
    .ALUCtl2(ALUCtl[2]), .ALUCtl1(ALUCtl[1]), .ALUCtl0(ALUCtl[0]));
  // Probe on PC
  // Probe on Branch
  // Probe on Jump
  // Probe on Jal
  // Probe on Jr
  // Probe on WrReg
  // Probe on WrAddr
  // Probe on multiplexer_6_out
  // Probe on MemWr
  // Probe on MemData
  and and_2 (Jr, comparator_3_eq, comparator_4_eq);

  // Other names for the same wires on the sheet: R_Type_Instruction (some bits) = {I_Type_Instruction, func};
  //   shamt[4:0] = R_Type_Instruction[10:6]; rd[4:0] = R_Type_Instruction[15:11]; rt[4:0] = I_Type_Instruction[20:16];
  //   rs[4:0] = I_Type_Instruction[25:21]; J_Type_Instruction[31:26] = I_Type_Instruction[31:26];
  //   op[5:0] = I_Type_Instruction[31:26]

  // Notes on the sheet:
  //   register to register arithmetic
  //   contents of rom_1 (hex, n*v repeats v):
  //   20010008 34220005 3043ffff 232020 832822 223024 663826 aca40064 8ca80064 22482a c95025 a95827
  //   161602b 296d0001 c000010 201b0001 200e0001 23ff001c 11c00003 1c97022 8000012 201c0001 3e00008
  //   201d0001 201e0001
  //   Immediate
endmodule

module ALU (
  input  [3:0] ALUCtl,
  input  [31:0] A,
  input  [31:0] B,
  input  [4:0] Shamt,
  output [31:0] ALUResult,
  output Zero,
  output Overflow
);

  wire comparator_1_lt, comparator_2_lt, comparator_3_eq, comparator_4_eq, or_2_out;
  wire [31:0] ADD, AND, NOR, OR, SLL, SLT, SLTU, SRL, SUB, XOR;

  // Probe on ALUCtl
  assign NOR = ~(A | B);  // NOR_Gate nor_1, 32 bits wide
  Adder #(.width(32)) adder_1 (.a(A), .b(B), .out(ADD));  // open: cin, cout
  Subtractor #(.width(32)) subtractor_1 (.a(A), .b(B), .out(SUB));  // open: bin, bout
  assign AND = A & B;  // AND_Gate and_1, 32 bits wide
  assign OR = A | B;  // OR_Gate or_1, 32 bits wide
  assign XOR = A ^ B;  // XOR_Gate xor_1, 32 bits wide
  Comparator #(.width(32)) comparator_1 (.a(A), .b(B), .lt(comparator_1_lt));  // open: gt, eq
  assign SLT = {{31{1'b0}}, comparator_1_lt};  // Bit_Extender bit_extender_1
  Shifter #(.width(32)) shifter_1 (.in(B), .\dist (Shamt), .out(SLL));
  Shifter #(.width(32), .shift("lr")) shifter_2 (.in(B), .\dist (Shamt), .out(SRL));
  Comparator #(.width(32), .mode("unsigned")) comparator_2 (.a(A), .b(B), .lt(comparator_2_lt));  // open: gt, eq
  assign SLTU = {{31{1'b0}}, comparator_2_lt};  // Bit_Extender bit_extender_2
  Multiplexer #(.select(4), .width(32), .enable("false")) multiplexer_1 (
    .in0(XOR), .in1(SLTU), .in2(SLT), .in3(AND), .in4(NOR), .in5(SUB), .in6(OR), .in7(ADD), .in8(SRL),
    .in9(SLL), .out(ALUResult), .sel(ALUCtl));  // open: in10, in11, in12, in13, in14, in15
  Comparator #(.width(4)) comparator_3 (.a(4'b0111), .b(ALUCtl), .eq(comparator_3_eq));  // open: gt, lt
  Comparator #(.width(4)) comparator_4 (.a(ALUCtl), .b(4'b0101), .eq(comparator_4_eq));  // open: gt, lt
  Overflow_Unit overflow_unit_1 (
    .Add(comparator_3_eq), .Sub(comparator_4_eq), .ASign(A[31]), .BSign(B[31]), .ResultSign(ALUResult[31]),
    .Overflow(Overflow));
  not not_1 (Zero, or_2_out);
  or or_2 (or_2_out, ALUResult[0], ALUResult[1], ALUResult[2], ALUResult[3], ALUResult[4], ALUResult[5], ALUResult[6], ALUResult[7], ALUResult[8], ALUResult[9], ALUResult[10], ALUResult[11], ALUResult[12], ALUResult[13], ALUResult[14], ALUResult[15], ALUResult[16], ALUResult[17], ALUResult[18], ALUResult[19], ALUResult[20], ALUResult[21], ALUResult[22], ALUResult[23], ALUResult[24], ALUResult[25], ALUResult[26], ALUResult[27], ALUResult[28], ALUResult[29], ALUResult[30], ALUResult[31]);

  // Other names for the same wires on the sheet: ASign = A[31]; ResultSign = ALUResult[31]; BSign = B[31]

  // Notes on the sheet:
  //   ALUCtl for ADD for top port
  //   ALUCtl for SUB for second port
endmodule

module Register_File (
  input  [4:0] WrAddr,
  input  [31:0] WrData,
  input  WrReg,
  input  [4:0] RdAddr1,
  input  [4:0] RdAddr2,
  input  Clock,
  output [31:0] RdData1,
  output [31:0] RdData2
);

  wire WrReg0, WrReg1, WrReg2, WrReg3, WrReg4, WrReg5, WrReg6, WrReg7, WrReg8, WrReg9, WrReg10, WrReg11,
       WrReg12, WrReg13, WrReg14, WrReg15, WrReg16, WrReg17, WrReg18, WrReg19, WrReg20, WrReg21, WrReg22,
       WrReg23, WrReg24, WrReg25, WrReg26, WrReg27, WrReg28, WrReg29, WrReg30, WrReg31;
  wire [31:0] RegData1, RegData2, RegData3, RegData4, RegData5, RegData6, RegData7, RegData8, RegData9,
       RegData10, RegData11, RegData12, RegData13, RegData14, RegData15, RegData16, RegData17, RegData18,
       RegData19, RegData20, RegData21, RegData22, RegData23, RegData24, RegData25, RegData26, RegData27,
       RegData28, RegData29, RegData30, RegData31;

  Demultiplexer #(.select(5), .enable("false")) demultiplexer_1 (
    .out0(WrReg0), .out1(WrReg1), .out2(WrReg2), .out3(WrReg3), .out4(WrReg4), .out5(WrReg5), .out6(WrReg6),
    .out7(WrReg7), .out8(WrReg8), .out9(WrReg9), .out10(WrReg10), .out11(WrReg11), .out12(WrReg12),
    .out13(WrReg13), .out14(WrReg14), .out15(WrReg15), .out16(WrReg16), .out17(WrReg17), .out18(WrReg18),
    .out19(WrReg19), .out20(WrReg20), .out21(WrReg21), .out22(WrReg22), .out23(WrReg23), .out24(WrReg24),
    .out25(WrReg25), .out26(WrReg26), .out27(WrReg27), .out28(WrReg28), .out29(WrReg29), .out30(WrReg30),
    .out31(WrReg31), .in(WrReg), .sel(WrAddr));
  // Probe on RegData4
  Register #(.width(32)) Reg4 (.D(WrData), .en(WrReg4), .Q(RegData4), .clk(Clock));  // open: clr
  // Probe on RegData8
  Register #(.width(32)) Reg8 (.D(WrData), .en(WrReg8), .Q(RegData8), .clk(Clock));  // open: clr
  // Probe on RegData12
  Register #(.width(32)) Reg12 (.D(WrData), .en(WrReg12), .Q(RegData12), .clk(Clock));  // open: clr
  // Probe on RegData16
  Register #(.width(32)) Reg16 (.D(WrData), .en(WrReg16), .Q(RegData16), .clk(Clock));  // open: clr
  // Probe on RegData20
  Register #(.width(32)) Reg20 (.D(WrData), .en(WrReg20), .Q(RegData20), .clk(Clock));  // open: clr
  // Probe on RegData24
  Register #(.width(32)) Reg24 (.D(WrData), .en(WrReg24), .Q(RegData24), .clk(Clock));  // open: clr
  // Probe on RegData28
  Register #(.width(32)) Reg28 (.D(WrData), .en(WrReg28), .Q(RegData28), .clk(Clock));  // open: clr
  Register #(.width(32)) Reg1 (.D(WrData), .en(WrReg1), .Q(RegData1), .clk(Clock));  // open: clr
  Register #(.width(32)) Reg5 (.D(WrData), .en(WrReg5), .Q(RegData5), .clk(Clock));  // open: clr
  Register #(.width(32)) Reg9 (.D(WrData), .en(WrReg9), .Q(RegData9), .clk(Clock));  // open: clr
  Register #(.width(32)) Reg13 (.D(WrData), .en(WrReg13), .Q(RegData13), .clk(Clock));  // open: clr
  Register #(.width(32)) Reg17 (.D(WrData), .en(WrReg17), .Q(RegData17), .clk(Clock));  // open: clr
  Register #(.width(32)) Reg21 (.D(WrData), .en(WrReg21), .Q(RegData21), .clk(Clock));  // open: clr
  Register #(.width(32)) Reg25 (.D(WrData), .en(WrReg25), .Q(RegData25), .clk(Clock));  // open: clr
  Register #(.width(32)) Reg29 (.D(WrData), .en(WrReg29), .Q(RegData29), .clk(Clock));  // open: clr
  // Probe on RegData1
  // Probe on RegData5
  // Probe on RegData9
  // Probe on RegData13
  // Probe on RegData17
  // Probe on RegData21
  // Probe on RegData25
  // Probe on RegData29
  // Probe on RegData2
  Register #(.width(32)) Reg2 (.D(WrData), .en(WrReg2), .Q(RegData2), .clk(Clock));  // open: clr
  // Probe on RegData6
  Register #(.width(32)) Reg6 (.D(WrData), .en(WrReg6), .Q(RegData6), .clk(Clock));  // open: clr
  // Probe on RegData10
  Register #(.width(32)) Reg10 (.D(WrData), .en(WrReg10), .Q(RegData10), .clk(Clock));  // open: clr
  // Probe on RegData14
  Register #(.width(32)) Reg14 (.D(WrData), .en(WrReg14), .Q(RegData14), .clk(Clock));  // open: clr
  // Probe on RegData18
  Register #(.width(32)) Reg18 (.D(WrData), .en(WrReg18), .Q(RegData18), .clk(Clock));  // open: clr
  // Probe on RegData22
  Register #(.width(32)) Reg22 (.D(WrData), .en(WrReg22), .Q(RegData22), .clk(Clock));  // open: clr
  // Probe on RegData26
  Register #(.width(32)) Reg26 (.D(WrData), .en(WrReg26), .Q(RegData26), .clk(Clock));  // open: clr
  // Probe on RegData30
  Register #(.width(32)) Reg30 (.D(WrData), .en(WrReg30), .Q(RegData30), .clk(Clock));  // open: clr
  // Probe on RegData3
  Register #(.width(32)) Reg3 (.D(WrData), .en(WrReg3), .Q(RegData3), .clk(Clock));  // open: clr
  // Probe on RegData7
  Register #(.width(32)) Reg7 (.D(WrData), .en(WrReg7), .Q(RegData7), .clk(Clock));  // open: clr
  // Probe on RegData11
  Register #(.width(32)) Reg11 (.D(WrData), .en(WrReg11), .Q(RegData11), .clk(Clock));  // open: clr
  // Probe on RegData15
  Register #(.width(32)) Reg15 (.D(WrData), .en(WrReg15), .Q(RegData15), .clk(Clock));  // open: clr
  // Probe on RegData19
  Register #(.width(32)) Reg19 (.D(WrData), .en(WrReg19), .Q(RegData19), .clk(Clock));  // open: clr
  // Probe on RegData23
  Register #(.width(32)) Reg23 (.D(WrData), .en(WrReg23), .Q(RegData23), .clk(Clock));  // open: clr
  // Probe on RegData27
  Register #(.width(32)) Reg27 (.D(WrData), .en(WrReg27), .Q(RegData27), .clk(Clock));  // open: clr
  // Probe on RegData31
  Register #(.width(32)) Reg31 (.D(WrData), .en(WrReg31), .Q(RegData31), .clk(Clock));  // open: clr
  Multiplexer #(.select(5), .width(32), .enable("false")) multiplexer_1 (
    .in0({32{1'b0}}), .in1(RegData1), .in2(RegData2), .in3(RegData3), .in4(RegData4), .in5(RegData5),
    .in6(RegData6), .in7(RegData7), .in8(RegData8), .in9(RegData9), .in10(RegData10), .in11(RegData11),
    .in12(RegData12), .in13(RegData13), .in14(RegData14), .in15(RegData15), .in16(RegData16),
    .in17(RegData17), .in18(RegData18), .in19(RegData19), .in20(RegData20), .in21(RegData21),
    .in22(RegData22), .in23(RegData23), .in24(RegData24), .in25(RegData25), .in26(RegData26),
    .in27(RegData27), .in28(RegData28), .in29(RegData29), .in30(RegData30), .in31(RegData31), .out(RdData1),
    .sel(RdAddr1));
  Multiplexer #(.select(5), .width(32), .enable("false")) multiplexer_2 (
    .in0({32{1'b0}}), .in1(RegData1), .in2(RegData2), .in3(RegData3), .in4(RegData4), .in5(RegData5),
    .in6(RegData6), .in7(RegData7), .in8(RegData8), .in9(RegData9), .in10(RegData10), .in11(RegData11),
    .in12(RegData12), .in13(RegData13), .in14(RegData14), .in15(RegData15), .in16(RegData16),
    .in17(RegData17), .in18(RegData18), .in19(RegData19), .in20(RegData20), .in21(RegData21),
    .in22(RegData22), .in23(RegData23), .in24(RegData24), .in25(RegData25), .in26(RegData26),
    .in27(RegData27), .in28(RegData28), .in29(RegData29), .in30(RegData30), .in31(RegData31), .out(RdData2),
    .sel(RdAddr2));
endmodule

module Overflow_Unit (
  input  Add,
  input  Sub,
  input  ASign,
  input  BSign,
  input  ResultSign,
  output Overflow
);

  wire and_1_out, and_2_out, or_1_out, xnor_1_out, xor_1_out, xor_2_out;

  xnor xnor_1 (xnor_1_out, ASign, BSign);
  xor xor_1 (xor_1_out, ASign, BSign);
  and and_1 (and_1_out, xnor_1_out, Add);
  and and_2 (and_2_out, xor_1_out, Sub);
  or or_1 (or_1_out, and_1_out, and_2_out);
  xor xor_2 (xor_2_out, ResultSign, ASign);
  and and_3 (Overflow, or_1_out, xor_2_out);

  // Notes on the sheet:
  //   Overflow occurs when doing addition and sign(A) == sign(B) && sign(result) != sign(A)
  //   Or
  //   Overflow occurs when doing subtraction and sign(A) != sign(B) && sign(result) != sign(A)
endmodule

module Jumps (
  output J,
  output JAL,
  output [31:0] out_3,
  output JALR,
  output JR,
  output ANDI,
  output ORI,
  output SLTI
);

  wire comparator_3_eq, comparator_4_eq, comparator_5_eq, comparator_6_eq;

  Comparator #(.width(6)) comparator_1 (.a(out_3[31:26]), .b(6'b000010), .eq(J));  // open: gt, lt
  Comparator #(.width(6)) comparator_2 (.a(out_3[31:26]), .b(6'b000011), .eq(JAL));  // open: gt, lt
  Comparator #(.width(6)) comparator_3 (.a(out_3[5:0]), .b(6'b001001), .eq(comparator_3_eq));  // open: gt, lt
  Comparator #(.width(6)) comparator_4 (.a(out_3[31:26]), .b({6{1'b0}}), .eq(comparator_4_eq));  // open: gt, lt
  Comparator #(.width(6)) comparator_5 (.a(out_3[5:0]), .b(6'b001000), .eq(comparator_5_eq));  // open: gt, lt
  Comparator #(.width(6)) comparator_6 (.a(out_3[31:26]), .b({6{1'b0}}), .eq(comparator_6_eq));  // open: gt, lt
  Comparator #(.width(6)) comparator_7 (.a(out_3[31:26]), .b(6'b001100), .eq(ANDI));  // open: gt, lt
  Comparator #(.width(6)) comparator_8 (.a(out_3[31:26]), .b(6'b001101), .eq(ORI));  // open: gt, lt
  Comparator #(.width(6)) comparator_9 (.a(out_3[31:26]), .b(6'b001010), .eq(SLTI));  // open: gt, lt
  and and_1 (JALR, comparator_3_eq, comparator_4_eq);
  and and_2 (JR, comparator_5_eq, comparator_6_eq);

  // Other names for the same wires on the sheet: func[5:0] = out_3[5:0]; op[5:0] = out_3[31:26]
endmodule

module Main_Control_Unit (
  input  Op5,
  input  Op4,
  input  Op3,
  input  Op2,
  input  Op1,
  input  Op0,
  output RegDst1,
  output RegDst0,
  output ALUSrc,
  output MemtoReg1,
  output MemtoReg0,
  output WrReg,
  output MemRead,
  output MemWrite,
  output Branch,
  output ALUOp1,
  output ALUOp2,
  output Jump
);

  wire and_5_out, and_6_out, and_7_out, not_1_out, not_2_out, not_3_out, not_4_out, not_5_out, not_6_out,
       not_7_out, not_8_out, not_9_out, not_10_out, not_11_out, not_12_out, not_13_out, not_14_out,
       not_15_out;

  not not_1 (not_1_out, Op5);
  not not_2 (not_2_out, Op3);
  not not_3 (not_3_out, Op1);
  or or_1 (ALUSrc, Op1, Op3);
  not not_4 (not_4_out, Op5);
  not not_5 (not_5_out, Op2);
  not not_6 (not_6_out, Op1);
  not not_7 (not_7_out, Op3);
  not not_8 (not_8_out, Op1);
  not not_9 (not_9_out, Op3);
  and and_1 (MemWrite, Op3, Op1);
  not not_10 (not_10_out, Op3);
  not not_11 (not_11_out, Op3);
  not not_12 (not_12_out, Op2);
  not not_13 (not_13_out, Op1);
  not not_14 (not_14_out, Op3);
  not not_15 (not_15_out, Op5);
  and and_2 (RegDst1, not_1_out, Op1);
  and and_3 (RegDst0, not_2_out, not_3_out);
  and and_4 (MemtoReg1, not_4_out, Op1);
  and and_5 (and_5_out, not_5_out, not_6_out);
  and and_6 (and_6_out, not_7_out, Op0);
  and and_7 (and_7_out, Op3, not_8_out);
  and and_8 (MemRead, Op5, not_9_out);
  and and_9 (Branch, not_10_out, Op2);
  and and_10 (ALUOp1, not_11_out, not_12_out, not_13_out);
  and and_11 (ALUOp2, not_14_out, Op2);
  and and_12 (Jump, not_15_out, Op1);
  or or_2 (WrReg, and_5_out, and_6_out, and_7_out);

  assign MemtoReg0 = Op5;
endmodule

module Alu_Control_Unit (
  input  ALUOp1,
  input  ALUOp0,
  input  func5,
  input  func4,
  input  func3,
  input  func2,
  input  func1,
  input  func0,
  output ALUCtl3,
  output ALUCtl2,
  output ALUCtl1,
  output ALUCtl0
);

  wire and_1_out, and_2_out, and_3_out, and_4_out, and_5_out, and_6_out, and_7_out, and_8_out, not_1_out,
       not_2_out, not_3_out, not_4_out, not_5_out, not_6_out, not_7_out, not_8_out, not_9_out, not_10_out,
       not_11_out, not_12_out, not_13_out, not_14_out, not_15_out, not_16_out;

  not not_1 (not_1_out, ALUOp1);
  not not_2 (not_2_out, func3);
  and and_1 (and_1_out, not_2_out, not_3_out);
  not not_3 (not_3_out, func2);
  not not_4 (not_4_out, func3);
  and and_2 (and_2_out, not_4_out, func0);
  not not_5 (not_5_out, ALUOp1);
  and and_3 (and_3_out, not_5_out, not_6_out);
  not not_6 (not_6_out, ALUOp0);
  not not_7 (not_7_out, ALUOp0);
  and and_4 (and_4_out, not_7_out, not_8_out);
  not not_8 (not_8_out, func1);
  not not_9 (not_9_out, ALUOp0);
  and and_5 (and_5_out, not_9_out, func3, not_10_out);
  not not_10 (not_10_out, func0);
  not not_11 (not_11_out, ALUOp1);
  not not_12 (not_12_out, func3);
  and and_6 (and_6_out, not_12_out, not_13_out);
  not not_13 (not_13_out, func2);
  not not_14 (not_14_out, func1);
  and and_7 (and_7_out, not_14_out, not_15_out);
  not not_15 (not_15_out, func0);
  not not_16 (not_16_out, func2);
  and and_8 (and_8_out, not_16_out, func0);
  or or_1 (ALUCtl2, not_1_out, and_1_out, and_2_out);
  or or_2 (ALUCtl1, and_3_out, and_4_out, and_5_out);
  or or_3 (ALUCtl0, not_11_out, and_6_out, and_7_out, and_8_out);

  assign ALUCtl3 = 1'b0;
endmodule

module ALU_CONTROL (
  input  ALUOp2,
  input  ALUOp1,
  input  ALUOp0,
  input  func5,
  input  func4,
  input  func3,
  input  func2,
  input  func1,
  input  func0,
  output ALUCtl3,
  output ALUCtl2,
  output ALUCtl1,
  output ALUCtl0
);

  wire and_1_out, and_2_out, and_3_out, and_4_out, and_5_out, and_6_out, and_7_out, and_8_out, and_9_out,
       and_10_out, and_11_out, and_12_out, and_13_out, and_14_out, and_15_out, and_16_out, not_1_out,
       not_2_out, not_3_out, not_4_out, not_5_out, not_6_out, not_7_out, not_8_out, not_9_out, not_10_out,
       not_11_out, not_12_out, not_13_out, not_14_out, not_15_out, not_16_out, not_17_out, not_18_out,
       not_19_out, not_20_out, not_21_out, not_22_out, not_23_out, not_24_out, not_25_out, not_26_out,
       not_27_out, not_28_out, not_29_out;

  not not_1 (not_1_out, ALUOp2);
  not not_2 (not_2_out, ALUOp1);
  not not_3 (not_3_out, ALUOp2);
  not not_4 (not_4_out, func3);
  not not_5 (not_5_out, func2);
  not not_6 (not_6_out, ALUOp2);
  not not_7 (not_7_out, func3);
  not not_8 (not_8_out, ALUOp2);
  not not_9 (not_9_out, ALUOp1);
  not not_10 (not_10_out, ALUOp1);
  not not_11 (not_11_out, ALUOp0);
  not not_12 (not_12_out, ALUOp0);
  not not_13 (not_13_out, func1);
  not not_14 (not_14_out, ALUOp0);
  not not_15 (not_15_out, func0);
  not not_16 (not_16_out, ALUOp2);
  not not_17 (not_17_out, ALUOp1);
  not not_18 (not_18_out, ALUOp0);
  not not_19 (not_19_out, ALUOp2);
  not not_20 (not_20_out, func3);
  not not_21 (not_21_out, func2);
  not not_22 (not_22_out, ALUOp2);
  not not_23 (not_23_out, func1);
  not not_24 (not_24_out, func0);
  not not_25 (not_25_out, ALUOp1);
  not not_26 (not_26_out, ALUOp0);
  not not_27 (not_27_out, ALUOp2);
  not not_28 (not_28_out, func2);
  not not_29 (not_29_out, ALUOp2);
  and and_1 (and_1_out, not_1_out, not_2_out);
  and and_2 (and_2_out, not_3_out, not_4_out, not_5_out);
  and and_3 (and_3_out, not_6_out, not_7_out, func0);
  and and_4 (and_4_out, not_8_out, ALUOp0);
  and and_5 (and_5_out, not_9_out, ALUOp0);
  and and_6 (and_6_out, not_10_out, not_11_out);
  and and_7 (and_7_out, not_12_out, not_13_out);
  and and_8 (and_8_out, not_14_out, func3, not_15_out);
  and and_9 (and_9_out, not_16_out, ALUOp1, ALUOp0);
  and and_10 (and_10_out, ALUOp2, not_17_out);
  and and_11 (and_11_out, ALUOp2, not_18_out);
  and and_12 (and_12_out, not_19_out, not_20_out, not_21_out);
  and and_13 (and_13_out, not_22_out, not_23_out, not_24_out);
  and and_14 (and_14_out, not_25_out, not_26_out);
  and and_15 (and_15_out, not_27_out, not_28_out, func0);
  and and_16 (and_16_out, not_29_out, ALUOp0);
  or or_1 (ALUCtl2, and_1_out, and_2_out, and_3_out, and_4_out, and_5_out);
  or or_2 (ALUCtl1, and_6_out, and_7_out, and_8_out, and_9_out, and_10_out, and_11_out);
  or or_3 (ALUCtl0, and_12_out, and_13_out, and_14_out, and_15_out, and_16_out);

  assign ALUCtl3 = 1'b0;
endmodule

module MAIN_CONTROL (
  input  op5,
  input  op4,
  input  op3,
  input  op2,
  input  op1,
  input  op0,
  output RegDst,
  output ALUSrc,
  output MemToReg,
  output RegWrite,
  output MemRead,
  output MemWrite,
  output Branch,
  output ALUOp2,
  output ALUOp1,
  output ALUOp0
);

  wire and_3_out, and_4_out, and_7_out, and_8_out, and_10_out, and_11_out, and_12_out, not_1_out, not_2_out,
       not_3_out, not_4_out, not_5_out, not_6_out, not_7_out, not_8_out, not_9_out, not_10_out, not_11_out,
       not_12_out, not_13_out, not_14_out;

  not not_1 (not_1_out, op3);
  not not_2 (not_2_out, op1);
  or or_1 (ALUSrc, op1, op3);
  not not_3 (not_3_out, op3);
  not not_4 (not_4_out, op2);
  not not_5 (not_5_out, op5);
  not not_6 (not_6_out, op3);
  and and_1 (MemWrite, op5, op3);
  not not_7 (not_7_out, op3);
  not not_8 (not_8_out, op0);
  not not_9 (not_9_out, op2);
  not not_10 (not_10_out, op0);
  not not_11 (not_11_out, op1);
  not not_12 (not_12_out, op3);
  not not_13 (not_13_out, op2);
  not not_14 (not_14_out, op1);
  and and_2 (RegDst, not_1_out, not_2_out);
  and and_3 (and_3_out, not_3_out, not_4_out);
  and and_4 (and_4_out, not_5_out, op3);
  and and_5 (MemRead, not_6_out, op1);
  and and_6 (Branch, not_7_out, op2);
  and and_7 (and_7_out, op1, not_8_out);
  and and_8 (and_8_out, op3, op2);
  and and_9 (ALUOp1, not_9_out, not_10_out);
  and and_10 (and_10_out, not_11_out, op0);
  and and_11 (and_11_out, not_12_out, op2);
  and and_12 (and_12_out, op3, not_13_out, not_14_out);
  or or_2 (RegWrite, and_3_out, and_4_out);
  or or_3 (ALUOp2, and_7_out, and_8_out);
  or or_4 (ALUOp0, and_10_out, and_11_out, and_12_out);

  assign MemToReg = op5;
endmodule

module JalMainControl (
  input  op5,
  input  op4,
  input  op3,
  input  op2,
  input  op1,
  input  op0,
  output RegDst,
  output RegDst0,
  output ALUSrc,
  output MemToReg,
  output MemToReg0,
  output RegWrite,
  output MemRead,
  output MemWrite,
  output Branch,
  output ALUOp2,
  output ALUOp1,
  output ALUOp0
);

  wire and_2_out, and_3_out, and_6_out, and_7_out, and_10_out, and_11_out, and_12_out, and_13_out,
       and_14_out, not_1_out, not_2_out, not_3_out, not_4_out, not_5_out, not_6_out, not_7_out, not_8_out,
       not_9_out, not_10_out, not_11_out, not_12_out, not_13_out;

  not not_1 (not_1_out, op3);
  not not_2 (not_2_out, op1);
  or or_1 (ALUSrc, op1, op3);
  not not_3 (not_3_out, op3);
  not not_4 (not_4_out, op2);
  not not_5 (not_5_out, op5);
  not not_6 (not_6_out, op3);
  and and_1 (MemWrite, op5, op3);
  not not_7 (not_7_out, op3);
  and and_2 (and_2_out, op3, op1);
  and and_3 (and_3_out, op3, op2);
  not not_8 (not_8_out, op2);
  not not_9 (not_9_out, op0);
  not not_10 (not_10_out, op2);
  not not_11 (not_11_out, op3);
  not not_12 (not_12_out, op2);
  not not_13 (not_13_out, op1);
  and and_4 (RegDst0, not_1_out, not_2_out);
  and and_5 (MemToReg, op1, op0);
  and and_6 (and_6_out, not_3_out, not_4_out);
  and and_7 (and_7_out, not_5_out, op3);
  and and_8 (MemRead, not_6_out, op1);
  and and_9 (Branch, not_7_out, op2);
  or or_2 (ALUOp2, and_2_out, and_3_out);
  and and_10 (and_10_out, not_8_out, not_9_out);
  and and_11 (and_11_out, op3, not_10_out);
  and and_12 (and_12_out, not_11_out, op2);
  and and_13 (and_13_out, op3, not_12_out, not_13_out);
  and and_14 (and_14_out, op3, op0);
  or or_3 (RegWrite, and_6_out, and_7_out);
  or or_4 (ALUOp1, and_10_out, and_11_out);
  or or_5 (ALUOp0, and_12_out, and_13_out, and_14_out);

  assign MemToReg0 = op5;
  assign RegDst = 1'b0;
endmodule
