// Logisim project Lab3.circ as structural Verilog: 7 circuits, main circuit Main
module Main (
  output [3:0] out_1
);

  wire ALUSrcA, and_1_out, andi, Clock, IorD, IRWrite, JAL, MemRead, MemWr, or_1_out, or_2_out, PCWrite,
       PCWriteCond, RegWrite, slti, Zero;
  wire [0:0] MemtoReg_0_1, RegDst_0_1;
  wire [1:0] ALUOp, ALUSrcB_0_1, PCSource_0_1;
  wire [3:0] State;
  wire [4:0] WrAddr;
  wire [5:0] func;
  wire [7:0] multiplexer_1_out;
  wire [31:0] A, a_t, adder_1_out, ALUout, ALUResult, ALUResultOut, B, b_t, MDR, multiplexer_7_out, PC,
       ram_1_data, register_file_1_rddata1, register_file_1_rddata2, Sign_Extend, SignExtShifted, WrData;
  wire [31:6] IR;

  Clock u_Clock (.out(Clock));
  and and_1 (and_1_out, Zero, PCWriteCond);
  or or_1 (or_1_out, PCWrite, and_1_out);
  control control_1 (
    .op5(IR[31]), .op4(IR[30]), .op3(IR[29]), .op2(IR[28]), .op1(IR[27]), .op0(IR[26]), .func5(func[5]),
    .func4(func[4]), .func3(func[3]), .func2(func[2]), .func1(func[1]), .func0(func[0]), .NS3(State[3]),
    .NS2(State[2]), .NS1(State[1]), .NS0(State[0]), .PCWrite(PCWrite), .PCWriteCond(PCWriteCond),
    .IorD(IorD), .MemRead(MemRead), .MemWrite(MemWr), .IRWrite(IRWrite), .MemtoReg0(MemtoReg_0_1[0]),
    .PCSource1(PCSource_0_1[1]), .PCSource0(PCSource_0_1[0]), .ALUOp1(ALUOp[1]), .ALUOp0(ALUOp[0]),
    .ALUSrcB1(ALUSrcB_0_1[1]), .ALUSrcB0(ALUSrcB_0_1[0]), .ALUSrcA(ALUSrcA), .RegWrite(RegWrite),
    .RegDst0(RegDst_0_1[0]), .Clock(Clock));
  // Probe on multiplexer_7_out
  Register #(.width(32)) PC_2 (.D(multiplexer_7_out), .en(or_1_out), .Q(PC), .clk(Clock));  // open: clr
  Multiplexer #(.width(8), .enable("false")) multiplexer_1 (
    .in0(PC[9:2]), .in1(ALUout[9:2]), .out(multiplexer_1_out), .sel(IorD));
  RAM #(.dataWidth(32), .bus("separate")) ram_1 (
    .addr(multiplexer_1_out), .din(B), .data(ram_1_data), .str(MemWr), .clk(Clock), .ld(MemRead));  // open: sel, clr
  Register #(.width(32)) u_IR (.D(ram_1_data), .en(IRWrite), .Q({IR, func}), .clk(Clock));  // open: clr
  Register #(.width(32)) u_MDR (.D(ram_1_data), .Q(MDR), .clk(Clock));  // open: en, clr
  Multiplexer #(.select(2), .width(5), .enable("false")) multiplexer_2 (
    .in0(IR[20:16]), .in1(IR[15:11]), .in2({5{1'b1}}), .out(WrAddr), .sel({1'b0, RegDst_0_1[0]}));  // open: in3
  Multiplexer #(.select(2), .width(32), .enable("false")) multiplexer_3 (
    .in0(ALUout), .in1(MDR), .in2(PC), .out(WrData), .sel({1'b0, MemtoReg_0_1[0]}));  // open: in3
  Register_File register_file_1 (
    .WrAddr(WrAddr), .WrData(WrData), .WrReg(RegWrite), .RdAddr1(IR[25:21]), .RdAddr2(IR[20:16]),
    .RdData1(register_file_1_rddata1), .RdData2(register_file_1_rddata2), .Clock(Clock));
  Comparator #(.width(6)) comparator_1 (.a(IR[31:26]), .b(6'b001100), .eq(andi));  // open: gt, lt
  Comparator #(.width(6)) comparator_2 (.a(IR[31:26]), .b(6'b001010), .eq(slti));  // open: gt, lt
  Register #(.width(32)) u_A (.D(register_file_1_rddata1), .Q(A), .clk(Clock));  // open: en, clr
  Register #(.width(32)) u_B (.D(register_file_1_rddata2), .Q(B), .clk(Clock));  // open: en, clr
  assign Sign_Extend = {{16{IR[15]}}, {IR[15:6], func}};  // Bit_Extender bit_extender_1
  Comparator #(.width(6)) comparator_3 (.a(IR[31:26]), .b(6'b000011), .eq(JAL));  // open: gt, lt
  Multiplexer #(.width(32), .enable("false")) multiplexer_4 (.in0(PC), .in1(A), .out(a_t), .sel(ALUSrcA));
  Multiplexer #(.select(2), .width(32), .enable("false")) multiplexer_5 (
    .in0(B), .in1(32'h4), .in2(Sign_Extend), .in3(SignExtShifted), .out(b_t), .sel(ALUSrcB_0_1));
  alu alu_1 (.Op(ALUOp), .Func(func), .Opcode(IR[31:26]), .state(State), .ALUCtrl(out_1));
  Adder #(.width(32)) adder_1 (.a(a_t), .b(b_t), .out(adder_1_out));  // open: cin, cout
  ALU alu_2 (.ALUCtl(out_1), .A(a_t), .B(b_t), .ALUResult(ALUResult), .Zero(Zero), .Shamt(IR[10:6]));  // open: Overflow
  Shifter #(.width(32)) shifter_1 (.in(Sign_Extend), .\dist (5'b00010), .out(SignExtShifted));
  or or_2 (or_2_out, andi, slti);
  Multiplexer #(.width(32), .enable("false")) multiplexer_6 (
    .in0(ALUResult), .in1(adder_1_out), .out(ALUResultOut), .sel(or_2_out));
  // Probe on ALUResult
  Multiplexer #(.select(2), .width(32), .enable("false")) multiplexer_7 (
    .in0(ALUResultOut), .in1(ALUout), .in2({PC[31:28], IR[25:6], func, 2'b00}), .in3(A),
    .out(multiplexer_7_out), .sel(PCSource_0_1));
  Register #(.width(32)) u_ALUout (.D(ALUResult), .Q(ALUout), .clk(Clock));  // open: en, clr
  // Probe on ALUResultOut
  // Probe on State
  // Probe on PC
  // Probe on RegWrite
  // Probe on WrAddr
  // Probe on WrData
  // Probe on MemWr
  // Probe on B
  // Probe on MemRead

  // Other names for the same wires on the sheet: ALUCtl[3:0] = out_1; op[5:0] = IR[31:26]; MemData[31:0] = B;
  //   IR[5:0] = func; PCShifted[31:2] = {PC[31:28], IR[25:6], func}; shamt[4:0] = IR[10:6]; rd[4:0] = IR[15:11];
  //   rt[4:0] = IR[20:16]; rs[4:0] = IR[25:21]

  // Notes on the sheet:
  //   Sorry for so many pins, I was debugging for so long! - MM
  //   Shifting the PC, takes bits 0-25 and shift them to 2-27, 
  //   Top of PC is included, and 0 constants for lower 2 bits
  //   We had 4 bit ALUOp before, so instead of redoing, we just zeroed the msb
  //   CONTROL UNIT
  //   Zero Constant is to compensate for our mistakes (Turns out we don't need that many bits).
  //   Instruction...
  //   andi
  //   slti
  //   It should just increment the PC regularly after an I instruction
  //   These are for debugging.  For some reason, the PC resets to zero after an I instruction, so I included these checks
  //   Jal forces us to increase mux, so do a special check instead
  //   ALU Control, only needed 2 ALUOp bits this time!
  //   Sign extend for mux input 2, then shift it for mux input 3
endmodule

module ALU (
  input  [3:0] ALUCtl,
  input  [31:0] A,
  input  [31:0] B,
  input  [4:0] Shamt,
  output [31:0] ALUResult,
  output Zero,
  output Overflow
);

  wire comparator_1_lt, comparator_2_lt, comparator_3_eq, comparator_4_eq, or_2_out;
  wire [31:0] ADD, AND, NOR, OR, SLL, SLT, SLTU, SRL, SUB, XOR;

  // Probe on ALUCtl
  assign NOR = ~(A | B);  // NOR_Gate nor_1, 32 bits wide
  Adder #(.width(32)) adder_1 (.a(A), .b(B), .out(ADD));  // open: cin, cout
  Subtractor #(.width(32)) subtractor_1 (.a(A), .b(B), .out(SUB));  // open: bin, bout
  assign AND = A & B;  // AND_Gate and_1, 32 bits wide
  assign OR = A | B;  // OR_Gate or_1, 32 bits wide
  assign XOR = A ^ B;  // XOR_Gate xor_1, 32 bits wide
  Comparator #(.width(32)) comparator_1 (.a(A), .b(B), .lt(comparator_1_lt));  // open: gt, eq
  assign SLT = {{31{1'b0}}, comparator_1_lt};  // Bit_Extender bit_extender_1
  Shifter #(.width(32)) shifter_1 (.in(B), .\dist (Shamt), .out(SLL));
  Shifter #(.width(32), .shift("lr")) shifter_2 (.in(B), .\dist (Shamt), .out(SRL));
  Comparator #(.width(32), .mode("unsigned")) comparator_2 (.a(A), .b(B), .lt(comparator_2_lt));  // open: gt, eq
  assign SLTU = {{31{1'b0}}, comparator_2_lt};  // Bit_Extender bit_extender_2
  Multiplexer #(.select(4), .width(32), .enable("false")) multiplexer_1 (
    .in0(XOR), .in1(SLTU), .in2(SLT), .in3(AND), .in4(NOR), .in5(SUB), .in6(OR), .in7(ADD), .in8(SRL),
    .in9(SLL), .out(ALUResult), .sel(ALUCtl));  // open: in10, in11, in12, in13, in14, in15
  Comparator #(.width(4)) comparator_3 (.a(4'b0111), .b(ALUCtl), .eq(comparator_3_eq));  // open: gt, lt
  Comparator #(.width(4)) comparator_4 (.a(ALUCtl), .b(4'b0101), .eq(comparator_4_eq));  // open: gt, lt
  Overflow_Unit overflow_unit_1 (
    .Add(comparator_3_eq), .Sub(comparator_4_eq), .ASign(A[31]), .BSign(B[31]), .ResultSign(ALUResult[31]),
    .Overflow(Overflow));
  or or_2 (or_2_out, ALUResult[0], ALUResult[1], ALUResult[2], ALUResult[3], ALUResult[4], ALUResult[5], ALUResult[6], ALUResult[7], ALUResult[8], ALUResult[9], ALUResult[10], ALUResult[11], ALUResult[12], ALUResult[13], ALUResult[14], ALUResult[15], ALUResult[16], ALUResult[17], ALUResult[18], ALUResult[19], ALUResult[20], ALUResult[21], ALUResult[22], ALUResult[23], ALUResult[24], ALUResult[25], ALUResult[26], ALUResult[27], ALUResult[28], ALUResult[29], ALUResult[30], ALUResult[31]);
  not not_1 (Zero, or_2_out);

  // Other names for the same wires on the sheet: ASign = A[31]; ResultSign = ALUResult[31]; BSign = B[31]

  // Notes on the sheet:
  //   ALUCtl for ADD for top port
  //   ALUCtl for SUB for second port
endmodule

module Register_File (
  input  [4:0] WrAddr,
  input  [31:0] WrData,
  input  WrReg,
  input  [4:0] RdAddr1,
  input  [4:0] RdAddr2,
  input  Clock,
  output [31:0] RdData1,
  output [31:0] RdData2
);

  wire WrReg0, WrReg1, WrReg2, WrReg3, WrReg4, WrReg5, WrReg6, WrReg7, WrReg8, WrReg9, WrReg10, WrReg11,
       WrReg12, WrReg13, WrReg14, WrReg15, WrReg16, WrReg17, WrReg18, WrReg19, WrReg20, WrReg21, WrReg22,
       WrReg23, WrReg24, WrReg25, WrReg26, WrReg27, WrReg28, WrReg29, WrReg30, WrReg31;
  wire [31:0] RegData1, RegData2, RegData3, RegData4, RegData5, RegData6, RegData7, RegData8, RegData9,
       RegData10, RegData11, RegData12, RegData13, RegData14, RegData15, RegData16, RegData17, RegData18,
       RegData19, RegData20, RegData21, RegData22, RegData23, RegData24, RegData25, RegData26, RegData27,
       RegData28, RegData29, RegData30, RegData31;

  Demultiplexer #(.select(5), .enable("false")) demultiplexer_1 (
    .out0(WrReg0), .out1(WrReg1), .out2(WrReg2), .out3(WrReg3), .out4(WrReg4), .out5(WrReg5), .out6(WrReg6),
    .out7(WrReg7), .out8(WrReg8), .out9(WrReg9), .out10(WrReg10), .out11(WrReg11), .out12(WrReg12),
    .out13(WrReg13), .out14(WrReg14), .out15(WrReg15), .out16(WrReg16), .out17(WrReg17), .out18(WrReg18),
    .out19(WrReg19), .out20(WrReg20), .out21(WrReg21), .out22(WrReg22), .out23(WrReg23), .out24(WrReg24),
    .out25(WrReg25), .out26(WrReg26), .out27(WrReg27), .out28(WrReg28), .out29(WrReg29), .out30(WrReg30),
    .out31(WrReg31), .in(WrReg), .sel(WrAddr));
  // Probe on RegData4
  Register #(.width(32)) Reg4 (.D(WrData), .en(WrReg4), .Q(RegData4), .clk(Clock));  // open: clr
  // Probe on RegData8
  Register #(.width(32)) Reg8 (.D(WrData), .en(WrReg8), .Q(RegData8), .clk(Clock));  // open: clr
  // Probe on RegData12
  Register #(.width(32)) Reg12 (.D(WrData), .en(WrReg12), .Q(RegData12), .clk(Clock));  // open: clr
  // Probe on RegData16
  Register #(.width(32)) Reg16 (.D(WrData), .en(WrReg16), .Q(RegData16), .clk(Clock));  // open: clr
  // Probe on RegData20
  Register #(.width(32)) Reg20 (.D(WrData), .en(WrReg20), .Q(RegData20), .clk(Clock));  // open: clr
  // Probe on RegData24
  Register #(.width(32)) Reg24 (.D(WrData), .en(WrReg24), .Q(RegData24), .clk(Clock));  // open: clr
  // Probe on RegData28
  Register #(.width(32)) Reg28 (.D(WrData), .en(WrReg28), .Q(RegData28), .clk(Clock));  // open: clr
  Register #(.width(32)) Reg1 (.D(WrData), .en(WrReg1), .Q(RegData1), .clk(Clock));  // open: clr
  Register #(.width(32)) Reg5 (.D(WrData), .en(WrReg5), .Q(RegData5), .clk(Clock));  // open: clr
  Register #(.width(32)) Reg9 (.D(WrData), .en(WrReg9), .Q(RegData9), .clk(Clock));  // open: clr
  Register #(.width(32)) Reg13 (.D(WrData), .en(WrReg13), .Q(RegData13), .clk(Clock));  // open: clr
  Register #(.width(32)) Reg17 (.D(WrData), .en(WrReg17), .Q(RegData17), .clk(Clock));  // open: clr
  Register #(.width(32)) Reg21 (.D(WrData), .en(WrReg21), .Q(RegData21), .clk(Clock));  // open: clr
  Register #(.width(32)) Reg25 (.D(WrData), .en(WrReg25), .Q(RegData25), .clk(Clock));  // open: clr
  Register #(.width(32)) Reg29 (.D(WrData), .en(WrReg29), .Q(RegData29), .clk(Clock));  // open: clr
  // Probe on RegData1
  // Probe on RegData5
  // Probe on RegData9
  // Probe on RegData13
  // Probe on RegData17
  // Probe on RegData21
  // Probe on RegData25
  // Probe on RegData29
  // Probe on RegData2
  Register #(.width(32)) Reg2 (.D(WrData), .en(WrReg2), .Q(RegData2), .clk(Clock));  // open: clr
  // Probe on RegData6
  Register #(.width(32)) Reg6 (.D(WrData), .en(WrReg6), .Q(RegData6), .clk(Clock));  // open: clr
  // Probe on RegData10
  Register #(.width(32)) Reg10 (.D(WrData), .en(WrReg10), .Q(RegData10), .clk(Clock));  // open: clr
  // Probe on RegData14
  Register #(.width(32)) Reg14 (.D(WrData), .en(WrReg14), .Q(RegData14), .clk(Clock));  // open: clr
  // Probe on RegData18
  Register #(.width(32)) Reg18 (.D(WrData), .en(WrReg18), .Q(RegData18), .clk(Clock));  // open: clr
  // Probe on RegData22
  Register #(.width(32)) Reg22 (.D(WrData), .en(WrReg22), .Q(RegData22), .clk(Clock));  // open: clr
  // Probe on RegData26
  Register #(.width(32)) Reg26 (.D(WrData), .en(WrReg26), .Q(RegData26), .clk(Clock));  // open: clr
  // Probe on RegData30
  Register #(.width(32)) Reg30 (.D(WrData), .en(WrReg30), .Q(RegData30), .clk(Clock));  // open: clr
  // Probe on RegData3
  Register #(.width(32)) Reg3 (.D(WrData), .en(WrReg3), .Q(RegData3), .clk(Clock));  // open: clr
  // Probe on RegData7
  Register #(.width(32)) Reg7 (.D(WrData), .en(WrReg7), .Q(RegData7), .clk(Clock));  // open: clr
  // Probe on RegData11
  Register #(.width(32)) Reg11 (.D(WrData), .en(WrReg11), .Q(RegData11), .clk(Clock));  // open: clr
  // Probe on RegData15
  Register #(.width(32)) Reg15 (.D(WrData), .en(WrReg15), .Q(RegData15), .clk(Clock));  // open: clr
  // Probe on RegData19
  Register #(.width(32)) Reg19 (.D(WrData), .en(WrReg19), .Q(RegData19), .clk(Clock));  // open: clr
  // Probe on RegData23
  Register #(.width(32)) Reg23 (.D(WrData), .en(WrReg23), .Q(RegData23), .clk(Clock));  // open: clr
  // Probe on RegData27
  Register #(.width(32)) Reg27 (.D(WrData), .en(WrReg27), .Q(RegData27), .clk(Clock));  // open: clr
  // Probe on RegData31
  Register #(.width(32)) Reg31 (.D(WrData), .en(WrReg31), .Q(RegData31), .clk(Clock));  // open: clr
  Multiplexer #(.select(5), .width(32), .enable("false")) multiplexer_1 (
    .in0({32{1'b0}}), .in1(RegData1), .in2(RegData2), .in3(RegData3), .in4(RegData4), .in5(RegData5),
    .in6(RegData6), .in7(RegData7), .in8(RegData8), .in9(RegData9), .in10(RegData10), .in11(RegData11),
    .in12(RegData12), .in13(RegData13), .in14(RegData14), .in15(RegData15), .in16(RegData16),
    .in17(RegData17), .in18(RegData18), .in19(RegData19), .in20(RegData20), .in21(RegData21),
    .in22(RegData22), .in23(RegData23), .in24(RegData24), .in25(RegData25), .in26(RegData26),
    .in27(RegData27), .in28(RegData28), .in29(RegData29), .in30(RegData30), .in31(RegData31), .out(RdData1),
    .sel(RdAddr1));
  Multiplexer #(.select(5), .width(32), .enable("false")) multiplexer_2 (
    .in0({32{1'b0}}), .in1(RegData1), .in2(RegData2), .in3(RegData3), .in4(RegData4), .in5(RegData5),
    .in6(RegData6), .in7(RegData7), .in8(RegData8), .in9(RegData9), .in10(RegData10), .in11(RegData11),
    .in12(RegData12), .in13(RegData13), .in14(RegData14), .in15(RegData15), .in16(RegData16),
    .in17(RegData17), .in18(RegData18), .in19(RegData19), .in20(RegData20), .in21(RegData21),
    .in22(RegData22), .in23(RegData23), .in24(RegData24), .in25(RegData25), .in26(RegData26),
    .in27(RegData27), .in28(RegData28), .in29(RegData29), .in30(RegData30), .in31(RegData31), .out(RdData2),
    .sel(RdAddr2));
endmodule

module Overflow_Unit (
  input  Add,
  input  Sub,
  input  ASign,
  input  BSign,
  input  ResultSign,
  output Overflow
);

  wire and_1_out, and_2_out, or_1_out, xnor_1_out, xor_1_out, xor_2_out;

  xnor xnor_1 (xnor_1_out, ASign, BSign);
  xor xor_1 (xor_1_out, ASign, BSign);
  and and_1 (and_1_out, xnor_1_out, Add);
  and and_2 (and_2_out, xor_1_out, Sub);
  or or_1 (or_1_out, and_1_out, and_2_out);
  xor xor_2 (xor_2_out, ResultSign, ASign);
  and and_3 (Overflow, or_1_out, xor_2_out);

  // Notes on the sheet:
  //   Overflow occurs when doing addition and sign(A) == sign(B) && sign(result) != sign(A)
  //   Or
  //   Overflow occurs when doing subtraction and sign(A) != sign(B) && sign(result) != sign(A)
endmodule

module Control_Unit (
  input  op5,
  input  op4,
  input  op3,
  input  op2,
  input  op1,
  input  op0,
  input  Clock,
  output PCWrite,
  output PCWriteCond,
  output IorD,
  output MemRead,
  output MemWrite,
  output IRWrite,
  output MemtoReg1,
  output MemtoReg0,
  output PCSource1,
  output PCSource0,
  output ALUOp3,
  output ALUOp2,
  output ALUOp1,
  output ALUOp0,
  output ALUSrcB1,
  output ALUSrcB0,
  output ALUSrcA,
  output RegWrite,
  output RegDst1,
  output RegDst0,
  output NS3,
  output NS2,
  output NS1,
  output NS0
);

  wire not_1_out, not_2_out, not_3_out, not_4_out, not_5_out, not_6_out;
  wire [1:0] AddrCtrl;
  wire [3:0] adder_1_out, rom_1_data, rom_2_data, State;

  not not_1 (not_1_out, op5);
  not not_2 (not_2_out, op4);
  not not_3 (not_3_out, op3);
  not not_4 (not_4_out, op2);
  not not_5 (not_5_out, op1);
  not not_6 (not_6_out, op0);
  // Probe on {op5, op4, op3, op2, op1, op0}
  // Probe on {NS3, NS2, NS1, NS0}
  Register #(.width(4)) u_State (.D({NS3, NS2, NS1, NS0}), .Q(State), .clk(Clock));  // open: en, clr
  ROM #(.addrWidth(6), .dataWidth(4)) rom_1 (.addr({op5, op4, op3, op2, op1, op0}), .data(rom_1_data));  // open: sel
  ROM #(.addrWidth(6), .dataWidth(4)) rom_2 (.addr({op5, op4, op3, op2, op1, op0}), .data(rom_2_data));  // open: sel
  Adder #(.width(4)) adder_1 (.a(4'b0001), .b(State), .out(adder_1_out));  // open: cin, cout
  Multiplexer #(.select(2), .width(4), .enable("false")) multiplexer_1 (
    .in0(4'b0000), .in1(rom_1_data), .in2(rom_2_data), .in3(adder_1_out), .out({NS3, NS2, NS1, NS0}),
    .sel(AddrCtrl));
  ROM #(.addrWidth(4), .dataWidth(2)) rom_3 (.addr(State), .data(AddrCtrl));  // open: sel
  ROM #(.addrWidth(4), .dataWidth(20)) rom_4 (
    .addr(State),
    .data({PCWrite, PCWriteCond, IorD, MemRead, MemWrite, IRWrite, MemtoReg1, MemtoReg0, PCSource1, PCSource0, ALUOp3, ALUOp2, ALUOp1, ALUOp0, ALUSrcB1, ALUSrcB0, ALUSrcA, RegWrite, RegDst1, RegDst0}));  // open: sel

  // Other names for the same wires on the sheet: NextState[3:0] = {NS3, NS2, NS1, NS0}

  // Notes on the sheet:
  //   Dispatch ROM 1
  //   Dispatch ROM 2
  //   contents of rom_1 (hex, n*v repeats v):
  //   6 0 9 0 8 30*0 2 7*0 2
  //   contents of rom_2 (hex, n*v repeats v):
  //   35*0 3 7*0 5
  //   contents of rom_3 (hex, n*v repeats v):
  //   3 1 2 3 0 0 3 0 0 0 1
  //   contents of rom_4 (hex, n*v repeats v):
  //   94090 30 28 30000 1004 28000 88 5 40448 80800 e8 4
  //   ALL OUTPUTS
endmodule

module alu (
  input  [1:0] Op,
  input  [5:0] Func,
  input  [5:0] Opcode,
  input  [3:0] state,
  output [3:0] ALUCtrl
);

  wire comparator_1_eq, comparator_2_eq, comparator_3_eq, comparator_4_eq, comparator_5_eq, isI, not_1_out,
       or_1_out;
  wire [3:0] rom_1_data, rom_2_data;

  Comparator #(.width(6)) comparator_1 (.a(Opcode), .b(6'b001100), .eq(comparator_1_eq));  // open: gt, lt
  Comparator #(.width(6)) comparator_2 (.a(Opcode), .b(6'b001000), .eq(comparator_2_eq));  // open: gt, lt
  Comparator #(.width(6)) comparator_3 (.a(Opcode), .b(6'b001101), .eq(comparator_3_eq));  // open: gt, lt
  Comparator #(.width(6)) comparator_4 (.a(Opcode), .b(6'b001010), .eq(comparator_4_eq));  // open: gt, lt
  Comparator #(.width(4)) comparator_5 (.a(state), .b(4'b0000), .eq(comparator_5_eq));  // open: gt, lt
  or or_1 (or_1_out, comparator_1_eq, comparator_2_eq, comparator_3_eq, comparator_4_eq);
  not not_1 (not_1_out, comparator_5_eq);
  ROM #(.dataWidth(4)) rom_1 (.addr({Op, Func}), .data(rom_1_data));  // open: sel
  ROM #(.addrWidth(6), .dataWidth(4)) rom_2 (.addr(Opcode), .data(rom_2_data));  // open: sel
  Multiplexer #(.width(4), .enable("false")) multiplexer_1 (
    .in0(rom_1_data), .in1(rom_2_data), .out(ALUCtrl), .sel(isI));
  // Probe on isI
  and and_1 (isI, or_1_out, not_1_out);

  // Other names for the same wires on the sheet: op_t[5:0] = Opcode

  // Notes on the sheet:
  //   If I instruction, do these: 
  //   andi
  //   addi
  //   ori
  //   slti
  //   If R instruction, or SLL/SRL
  //   contents of rom_1 (hex, n*v repeats v):
  //   64*7 64*5 9 0 8 29*0 7 0 5 0 3 6 0 4 0 0 2 1
  //   contents of rom_2 (hex, n*v repeats v):
  //   8*0 7 0 2 0 3 6
  //   not State 0
  //   If is an I instruction, then perform the bottom rom
endmodule

module control (
  input  op5,
  input  op4,
  input  op3,
  input  op2,
  input  op1,
  input  op0,
  input  func5,
  input  func4,
  input  func3,
  input  func2,
  input  func1,
  input  func0,
  input  Clock,
  output PCWrite,
  output PCWriteCond,
  output IorD,
  output MemRead,
  output MemWrite,
  output IRWrite,
  output MemtoReg0,
  output PCSource1,
  output PCSource0,
  output ALUOp1,
  output ALUOp0,
  output ALUSrcB1,
  output ALUSrcB0,
  output ALUSrcA,
  output RegWrite,
  output RegDst0,
  output NS3,
  output NS2,
  output NS1,
  output NS0
);

  wire comparator_1_eq, comparator_2_eq, JR, not_1_out, not_2_out, not_3_out, not_4_out, not_5_out, not_6_out;
  wire [1:0] AddrCtrl;
  wire [3:0] adder_1_out, multiplexer_1_out, rom_1_data, rom_2_data, State;

  not not_1 (not_1_out, op5);
  not not_2 (not_2_out, op4);
  not not_3 (not_3_out, op3);
  not not_4 (not_4_out, op2);
  not not_5 (not_5_out, op1);
  not not_6 (not_6_out, op0);
  Comparator #(.width(6)) comparator_1 (
    .a({op5, op4, op3, op2, op1, op0}), .b({6{1'b0}}), .eq(comparator_1_eq));  // open: gt, lt
  Comparator #(.width(6)) comparator_2 (
    .a({func5, func4, func3, func2, func1, func0}), .b(6'b001000), .eq(comparator_2_eq));  // open: gt, lt
  and and_1 (JR, comparator_1_eq, comparator_2_eq);
  // Probe on {NS3, NS2, NS1, NS0}
  Register #(.width(4)) u_State (.D({NS3, NS2, NS1, NS0}), .Q(State), .clk(Clock));  // open: en, clr
  ROM #(.addrWidth(6), .dataWidth(4)) rom_1 (.addr({op5, op4, op3, op2, op1, op0}), .data(rom_1_data));  // open: sel
  ROM #(.addrWidth(6), .dataWidth(4)) rom_2 (.addr({op5, op4, op3, op2, op1, op0}), .data(rom_2_data));  // open: sel
  Multiplexer #(.width(4), .enable("false")) multiplexer_1 (
    .in0(rom_1_data), .in1(4'b1011), .out(multiplexer_1_out), .sel(JR));
  Adder #(.width(4)) adder_1 (.a(4'b0001), .b(State), .out(adder_1_out));  // open: cin, cout
  ROM #(.addrWidth(4), .dataWidth(2)) rom_3 (.addr(State), .data(AddrCtrl));  // open: sel
  ROM #(.addrWidth(4), .dataWidth(16)) rom_4 (
    .addr(State),
    .data({PCWrite, PCWriteCond, IorD, MemRead, MemWrite, IRWrite, MemtoReg0, PCSource1, PCSource0, ALUOp1, ALUOp0, ALUSrcB1, ALUSrcB0, ALUSrcA, RegWrite, RegDst0}));  // open: sel
  Multiplexer #(.select(2), .width(4), .enable("false")) multiplexer_2 (
    .in0(4'b0000), .in1(multiplexer_1_out), .in2(rom_2_data), .in3(adder_1_out), .out({NS3, NS2, NS1, NS0}),
    .sel(AddrCtrl));

  // Other names for the same wires on the sheet: NextState[3:0] = {NS3, NS2, NS1, NS0}

  // Notes on the sheet:
  //   Dispatch ROM 1
  //   Dispatch ROM 2
  //   contents of rom_1 (hex, n*v repeats v):
  //   6 0 9 a 8 0 0 0 c 0 c 0 c c 21*0 2 7*0 2
  //   contents of rom_2 (hex, n*v repeats v):
  //   35*0 3 7*0 5
  //   contents of rom_3 (hex, n*v repeats v):
  //   3 1 2 3 0 0 3 5*0 3
  //   ROM Implementation from Appendix C of Microcode
  //   contents of rom_4 (hex, n*v repeats v):
  //   9408 18 14 3000 202 2800 44 3 40a4 8100 8100 0 14 2
  //   ALL OUTPUTS
endmodule
