// Logisim project lab4WithControl.circ as structural Verilog: 6 circuits, main circuit Main
module Main (
);

  wire ALUSrc, AluSrc_t, Branch, Clock, EX_MEM_Zero_q, MemRead, MemWr, PCSrc, RegWrite, undriven_2, Zero;
  wire [1:0] MemtoReg, RegDst;
  wire [2:0] ALUOp;
  wire [3:0] ALUCtl;
  wire [4:0] EX_MEM_RegDst_q, ID_EX_rd_q, ID_EX_rt_q, multiplexer_3_out, rd, rs, rt, shamt, undriven, WrAddr;
  wire [5:0] func, op;
  wire [31:0] adder_1_out, adder_2_out, ALUResult, EX_MEM_ALUResult_q, EX_MEM_PC_q, EX_MEM_RdData2_q,
       ID_EX_PC_q, ID_EX_RdData1_q, ID_EX_RdData2_q, ID_EX_Sign_Extend_q, IF_ID_PC_q, Instruction,
       MEM_WB_MemRead_q, MEM_WB_ReadData_q, multiplexer_1_out, multiplexer_2_out, PC, ram_1_data,
       register_file_1_rddata1, register_file_1_rddata2, shifter_2_out, Sign_Extend, SignExtShifted, WrData;

  Register #(.width(32)) u_PC (.D(multiplexer_1_out), .Q(PC), .clk(Clock));  // open: en, clr
  Multiplexer #(.width(32), .enable("false")) multiplexer_1 (
    .in0(EX_MEM_PC_q), .in1(adder_1_out), .out(multiplexer_1_out), .sel(PCSrc));
  Clock u_Clock (.out(Clock));
  Adder #(.width(32)) adder_1 (.a(PC), .b(32'h4), .out(adder_1_out));  // open: cin, cout
  ROM #(.dataWidth(32)) rom_1 (.addr(PC[9:2]), .data(Instruction));  // open: sel
  Main_Control_Unit main_control_unit_1 (
    .op(op), .out_1(RegDst), .out_2(AluSrc_t), .out_3(MemtoReg), .out_4(RegWrite), .out_6(MemRead),
    .out_7(MemWr), .out_8(Branch), .out_9(ALUOp));
  ALU_Control_Unit alu_control_unit_1 (.ALUOp(ALUOp), .func(func), .ALUCtl(ALUCtl));
  Register #(.width(32)) IF_ID_PC (.D(adder_1_out), .Q(IF_ID_PC_q), .clk(Clock));  // open: en, clr
  Register #(.width(32)) IF_ID_Instr (
    .D(Instruction), .Q({op, rs, rt, rd, shamt, func}), .clk(Clock));  // open: en, clr
  Register_File register_file_1 (
    .WrAddr(WrAddr), .WrData(WrData), .WrReg(RegWrite), .RdAddr1(rs), .RdAddr2(rt),
    .RdData1(register_file_1_rddata1), .RdData2(register_file_1_rddata2));  // open: Clock
  assign Sign_Extend = {{16{Instruction[15]}}, Instruction[15:0]};  // Bit_Extender bit_extender_1
  Register #(.width(32)) ID_EX_PC (.D(IF_ID_PC_q), .Q(ID_EX_PC_q), .clk(Clock));  // open: en, clr
  Register #(.width(32)) ID_EX_RdData1 (
    .D(register_file_1_rddata1), .Q(ID_EX_RdData1_q), .clk(Clock));  // open: en, clr
  Register #(.width(32)) ID_EX_RdData2 (
    .D(register_file_1_rddata2), .Q(ID_EX_RdData2_q), .clk(Clock));  // open: en, clr
  Register #(.width(32)) ID_EX_Sign_Extend (.D(Sign_Extend), .Q(ID_EX_Sign_Extend_q), .clk(Clock));  // open: en, clr
  Register #(.width(5)) ID_EX_rt (.D(rt), .Q(ID_EX_rt_q), .clk(Clock));  // open: en, clr
  Register #(.width(5)) ID_EX_rd (.D(rd), .Q(ID_EX_rd_q), .clk(Clock));  // open: en, clr
  Multiplexer #(.width(32), .enable("false")) multiplexer_2 (
    .in0(ID_EX_RdData2_q), .in1(ID_EX_Sign_Extend_q), .out(multiplexer_2_out), .sel(ALUSrc));
  Shifter #(.width(32)) shifter_1 (.in(Sign_Extend), .\dist (5'b00010), .out(SignExtShifted));
  ALU alu_1 (
    .ALUCtl(ALUCtl), .A(ID_EX_RdData1_q), .B(multiplexer_2_out), .ALUResult(ALUResult), .Zero(Zero),
    .Shamt(undriven));  // open: Overflow
  Multiplexer #(.select(2), .width(5), .enable("false")) multiplexer_3 (
    .in0(ID_EX_rt_q), .in1(ID_EX_rd_q), .out(multiplexer_3_out), .sel(RegDst));  // open: in2, in3
  Shifter #(.width(32)) shifter_2 (.in(ID_EX_Sign_Extend_q), .\dist (5'b00010), .out(shifter_2_out));
  Adder #(.width(32)) adder_2 (.a(ID_EX_PC_q), .b(shifter_2_out), .out(adder_2_out));  // open: cin, cout
  Register #(.width(32)) EX_MEM_PC (.D(adder_2_out), .Q(EX_MEM_PC_q), .clk(Clock));  // open: en, clr
  Register #(.width(32)) EX_MEM_ALUResult (.D(ALUResult), .Q(EX_MEM_ALUResult_q), .clk(Clock));  // open: en, clr
  Register #(.width(32)) EX_MEM_RdData2 (.D(ID_EX_RdData2_q), .Q(EX_MEM_RdData2_q), .clk(Clock));  // open: en, clr
  Register #(.width(5)) EX_MEM_RegDst (.D(multiplexer_3_out), .Q(EX_MEM_RegDst_q), .clk(Clock));  // open: en, clr
  Register #(.width(1)) EX_MEM_Zero (.D(Zero), .Q(EX_MEM_Zero_q), .clk(Clock));  // open: en, clr
  and and_1 (PCSrc, Branch, EX_MEM_Zero_q);
  RAM #(.dataWidth(32), .bus("separate")) ram_1 (
    .addr(EX_MEM_ALUResult_q[9:2]), .din(EX_MEM_RdData2_q), .data(ram_1_data), .str(MemWr), .clk(Clock),
    .ld(MemRead));  // open: sel, clr
  Register #(.width(32)) MEM_WB_PC (.clk(Clock));  // open: D, en, Q, clr
  Register #(.width(32)) MEM_WB_ReadData (.D(ram_1_data), .Q(MEM_WB_ReadData_q), .clk(Clock));  // open: en, clr
  Register #(.width(32)) MEM_WB_MemRead (.D(EX_MEM_ALUResult_q), .Q(MEM_WB_MemRead_q), .clk(Clock));  // open: en, clr
  Register #(.width(5)) MEM_WB_RegDst (.D(EX_MEM_RegDst_q), .Q(WrAddr), .clk(Clock));  // open: en, clr
  Multiplexer #(.select(2), .width(32), .enable("false")) multiplexer_4 (
    .in0(MEM_WB_ReadData_q), .in1(MEM_WB_MemRead_q), .out(WrData), .sel(MemtoReg));  // open: in2, in3
  // Probe on PC
  // Probe on Branch
  // Probe on nothing
  // Probe on nothing
  // Probe on nothing
  // Probe on RegWrite
  // Probe on WrAddr
  // Probe on WrData
  // Probe on MemWr
  // Probe on undriven_2
  // Probe on MemRead

  // Notes on the sheet:
  //   Sign extend for mux input 2, then shift it for mux input 3
endmodule

module ALU (
  input  [3:0] ALUCtl,
  input  [31:0] A,
  input  [31:0] B,
  input  [4:0] Shamt,
  output [31:0] ALUResult,
  output Zero,
  output Overflow
);

  wire comparator_1_lt, comparator_2_lt, comparator_3_eq, comparator_4_eq, or_2_out;
  wire [31:0] ADD, AND, NOR, OR, SLL, SLT, SLTU, SRL, SUB, XOR;

  assign XOR = A ^ B;  // XOR_Gate xor_1, 32 bits wide
  Adder #(.width(32)) adder_1 (.a(A), .b(B), .out(ADD));  // open: cin, cout
  Subtractor #(.width(32)) subtractor_1 (.a(A), .b(B), .out(SUB));  // open: bin, bout
  assign AND = A & B;  // AND_Gate and_1, 32 bits wide
  assign OR = A | B;  // OR_Gate or_1, 32 bits wide
  assign NOR = ~(A | B);  // NOR_Gate nor_1, 32 bits wide
  Comparator #(.width(32)) comparator_1 (.a(A), .b(B), .lt(comparator_1_lt));  // open: gt, eq
  assign SLT = {{31{1'b0}}, comparator_1_lt};  // Bit_Extender bit_extender_1
  Shifter #(.width(32)) shifter_1 (.in(B), .\dist (Shamt), .out(SLL));
  Shifter #(.width(32), .shift("lr")) shifter_2 (.in(B), .\dist (Shamt), .out(SRL));
  Comparator #(.width(32), .mode("unsigned")) comparator_2 (.a(A), .b(B), .lt(comparator_2_lt));  // open: gt, eq
  assign SLTU = {{31{1'b0}}, comparator_2_lt};  // Bit_Extender bit_extender_2
  Multiplexer #(.select(4), .width(32), .enable("false")) multiplexer_1 (
    .in0(XOR), .in1(SLTU), .in2(SLT), .in3(AND), .in4(NOR), .in5(SUB), .in6(OR), .in7(ADD), .in8(SRL),
    .in9(SLL), .out(ALUResult), .sel(ALUCtl));  // open: in10, in11, in12, in13, in14, in15
  Comparator #(.width(4)) comparator_3 (.a(4'b0111), .b(ALUCtl), .eq(comparator_3_eq));  // open: gt, lt
  Comparator #(.width(4)) comparator_4 (.a(ALUCtl), .b(4'b0101), .eq(comparator_4_eq));  // open: gt, lt
  Overflow_Unit overflow_unit_1 (
    .Add(comparator_3_eq), .Sub(comparator_4_eq), .ASign(A[31]), .BSign(B[31]), .ResultSign(ALUResult[31]),
    .Overflow(Overflow));
  or or_2 (or_2_out, ALUResult[0], ALUResult[1], ALUResult[2], ALUResult[3], ALUResult[4], ALUResult[5], ALUResult[6], ALUResult[7], ALUResult[8], ALUResult[9], ALUResult[10], ALUResult[11], ALUResult[12], ALUResult[13], ALUResult[14], ALUResult[15], ALUResult[16], ALUResult[17], ALUResult[18], ALUResult[19], ALUResult[20], ALUResult[21], ALUResult[22], ALUResult[23], ALUResult[24], ALUResult[25], ALUResult[26], ALUResult[27], ALUResult[28], ALUResult[29], ALUResult[30], ALUResult[31]);
  not not_1 (Zero, or_2_out);

  // Other names for the same wires on the sheet: ASign = A[31]; ResultSign = ALUResult[31]; BSign = B[31]

  // Notes on the sheet:
  //   ALUCtl for ADD on top port
  //   ALUCtl for SUB on second port
endmodule

module Register_File (
  input  [4:0] WrAddr,
  input  [31:0] WrData,
  input  WrReg,
  input  [4:0] RdAddr1,
  input  [4:0] RdAddr2,
  input  Clock,
  output [31:0] RdData1,
  output [31:0] RdData2
);

  wire and_1_out, and_2_out, comparator_1_eq, comparator_2_eq, comparator_3_eq, comparator_4_eq, not_1_out,
       not_2_out, WrReg0, WrReg1, WrReg2, WrReg3, WrReg4, WrReg5, WrReg6, WrReg7, WrReg8, WrReg9, WrReg10,
       WrReg11, WrReg12, WrReg13, WrReg14, WrReg15, WrReg16, WrReg17, WrReg18, WrReg19, WrReg20, WrReg21,
       WrReg22, WrReg23, WrReg24, WrReg25, WrReg26, WrReg27, WrReg28, WrReg29, WrReg30, WrReg31;
  wire [31:0] multiplexer_1_out, multiplexer_2_out, RegData1, RegData2, RegData3, RegData4, RegData5,
       RegData6, RegData7, RegData8, RegData9, RegData10, RegData11, RegData12, RegData13, RegData14,
       RegData15, RegData16, RegData17, RegData18, RegData19, RegData20, RegData21, RegData22, RegData23,
       RegData24, RegData25, RegData26, RegData27, RegData28, RegData29, RegData30, RegData31;

  Demultiplexer #(.select(5), .enable("false")) demultiplexer_1 (
    .out0(WrReg0), .out1(WrReg1), .out2(WrReg2), .out3(WrReg3), .out4(WrReg4), .out5(WrReg5), .out6(WrReg6),
    .out7(WrReg7), .out8(WrReg8), .out9(WrReg9), .out10(WrReg10), .out11(WrReg11), .out12(WrReg12),
    .out13(WrReg13), .out14(WrReg14), .out15(WrReg15), .out16(WrReg16), .out17(WrReg17), .out18(WrReg18),
    .out19(WrReg19), .out20(WrReg20), .out21(WrReg21), .out22(WrReg22), .out23(WrReg23), .out24(WrReg24),
    .out25(WrReg25), .out26(WrReg26), .out27(WrReg27), .out28(WrReg28), .out29(WrReg29), .out30(WrReg30),
    .out31(WrReg31), .in(WrReg), .sel(WrAddr));
  // Probe on RegData4
  Register #(.width(32)) Reg4 (.D(WrData), .en(WrReg4), .Q(RegData4), .clk(Clock));  // open: clr
  // Probe on RegData8
  Register #(.width(32)) Reg8 (.D(WrData), .en(WrReg8), .Q(RegData8), .clk(Clock));  // open: clr
  // Probe on RegData12
  Register #(.width(32)) Reg12 (.D(WrData), .en(WrReg12), .Q(RegData12), .clk(Clock));  // open: clr
  // Probe on RegData16
  Register #(.width(32)) Reg16 (.D(WrData), .en(WrReg16), .Q(RegData16), .clk(Clock));  // open: clr
  // Probe on RegData20
  Register #(.width(32)) Reg20 (.D(WrData), .en(WrReg20), .Q(RegData20), .clk(Clock));  // open: clr
  // Probe on RegData24
  Register #(.width(32)) Reg24 (.D(WrData), .en(WrReg24), .Q(RegData24), .clk(Clock));  // open: clr
  // Probe on RegData28
  Register #(.width(32)) Reg28 (.D(WrData), .en(WrReg28), .Q(RegData28), .clk(Clock));  // open: clr
  Register #(.width(32)) Reg1 (.D(WrData), .en(WrReg1), .Q(RegData1), .clk(Clock));  // open: clr
  Register #(.width(32)) Reg5 (.D(WrData), .en(WrReg5), .Q(RegData5), .clk(Clock));  // open: clr
  Register #(.width(32)) Reg9 (.D(WrData), .en(WrReg9), .Q(RegData9), .clk(Clock));  // open: clr
  Register #(.width(32)) Reg13 (.D(WrData), .en(WrReg13), .Q(RegData13), .clk(Clock));  // open: clr
  Register #(.width(32)) Reg17 (.D(WrData), .en(WrReg17), .Q(RegData17), .clk(Clock));  // open: clr
  Register #(.width(32)) Reg21 (.D(WrData), .en(WrReg21), .Q(RegData21), .clk(Clock));  // open: clr
  Register #(.width(32)) Reg25 (.D(WrData), .en(WrReg25), .Q(RegData25), .clk(Clock));  // open: clr
  Register #(.width(32)) Reg29 (.D(WrData), .en(WrReg29), .Q(RegData29), .clk(Clock));  // open: clr
  // Probe on RegData1
  // Probe on RegData5
  // Probe on RegData9
  // Probe on RegData13
  // Probe on RegData17
  // Probe on RegData21
  // Probe on RegData25
  // Probe on RegData29
  // Probe on RegData2
  Register #(.width(32)) Reg2 (.D(WrData), .en(WrReg2), .Q(RegData2), .clk(Clock));  // open: clr
  // Probe on RegData6
  Register #(.width(32)) Reg6 (.D(WrData), .en(WrReg6), .Q(RegData6), .clk(Clock));  // open: clr
  // Probe on RegData10
  Register #(.width(32)) Reg10 (.D(WrData), .en(WrReg10), .Q(RegData10), .clk(Clock));  // open: clr
  // Probe on RegData14
  Register #(.width(32)) Reg14 (.D(WrData), .en(WrReg14), .Q(RegData14), .clk(Clock));  // open: clr
  // Probe on RegData18
  Register #(.width(32)) Reg18 (.D(WrData), .en(WrReg18), .Q(RegData18), .clk(Clock));  // open: clr
  // Probe on RegData22
  Register #(.width(32)) Reg22 (.D(WrData), .en(WrReg22), .Q(RegData22), .clk(Clock));  // open: clr
  // Probe on RegData26
  Register #(.width(32)) Reg26 (.D(WrData), .en(WrReg26), .Q(RegData26), .clk(Clock));  // open: clr
  // Probe on RegData30
  Register #(.width(32)) Reg30 (.D(WrData), .en(WrReg30), .Q(RegData30), .clk(Clock));  // open: clr
  // Probe on RegData3
  Register #(.width(32)) Reg3 (.D(WrData), .en(WrReg3), .Q(RegData3), .clk(Clock));  // open: clr
  // Probe on RegData7
  Register #(.width(32)) Reg7 (.D(WrData), .en(WrReg7), .Q(RegData7), .clk(Clock));  // open: clr
  // Probe on RegData11
  Register #(.width(32)) Reg11 (.D(WrData), .en(WrReg11), .Q(RegData11), .clk(Clock));  // open: clr
  // Probe on RegData15
  Register #(.width(32)) Reg15 (.D(WrData), .en(WrReg15), .Q(RegData15), .clk(Clock));  // open: clr
  // Probe on RegData19
  Register #(.width(32)) Reg19 (.D(WrData), .en(WrReg19), .Q(RegData19), .clk(Clock));  // open: clr
  // Probe on RegData23
  Register #(.width(32)) Reg23 (.D(WrData), .en(WrReg23), .Q(RegData23), .clk(Clock));  // open: clr
  // Probe on RegData27
  Register #(.width(32)) Reg27 (.D(WrData), .en(WrReg27), .Q(RegData27), .clk(Clock));  // open: clr
  // Probe on RegData31
  Register #(.width(32)) Reg31 (.D(WrData), .en(WrReg31), .Q(RegData31), .clk(Clock));  // open: clr
  Multiplexer #(.select(5), .width(32), .enable("false")) multiplexer_1 (
    .in0({32{1'b0}}), .in1(RegData1), .in2(RegData2), .in3(RegData3), .in4(RegData4), .in5(RegData5),
    .in6(RegData6), .in7(RegData7), .in8(RegData8), .in9(RegData9), .in10(RegData10), .in11(RegData11),
    .in12(RegData12), .in13(RegData13), .in14(RegData14), .in15(RegData15), .in16(RegData16),
    .in17(RegData17), .in18(RegData18), .in19(RegData19), .in20(RegData20), .in21(RegData21),
    .in22(RegData22), .in23(RegData23), .in24(RegData24), .in25(RegData25), .in26(RegData26),
    .in27(RegData27), .in28(RegData28), .in29(RegData29), .in30(RegData30), .in31(RegData31),
    .out(multiplexer_1_out), .sel(RdAddr1));
  Multiplexer #(.select(5), .width(32), .enable("false")) multiplexer_2 (
    .in0({32{1'b0}}), .in1(RegData1), .in2(RegData2), .in3(RegData3), .in4(RegData4), .in5(RegData5),
    .in6(RegData6), .in7(RegData7), .in8(RegData8), .in9(RegData9), .in10(RegData10), .in11(RegData11),
    .in12(RegData12), .in13(RegData13), .in14(RegData14), .in15(RegData15), .in16(RegData16),
    .in17(RegData17), .in18(RegData18), .in19(RegData19), .in20(RegData20), .in21(RegData21),
    .in22(RegData22), .in23(RegData23), .in24(RegData24), .in25(RegData25), .in26(RegData26),
    .in27(RegData27), .in28(RegData28), .in29(RegData29), .in30(RegData30), .in31(RegData31),
    .out(multiplexer_2_out), .sel(RdAddr2));
  Multiplexer #(.width(32), .enable("false")) multiplexer_3 (
    .in0(multiplexer_1_out), .in1(WrData), .out(RdData1), .sel(and_1_out));
  Comparator #(.width(5), .mode("unsigned")) comparator_1 (
    .a(WrAddr), .b(RdAddr2), .eq(comparator_1_eq));  // open: gt, lt
  Multiplexer #(.width(32), .enable("false")) multiplexer_4 (
    .in0(multiplexer_2_out), .in1(WrData), .out(RdData2), .sel(and_2_out));
  Comparator #(.width(5), .mode("unsigned")) comparator_2 (
    .a(WrAddr), .b(RdAddr1), .eq(comparator_2_eq));  // open: gt, lt
  and and_1 (and_1_out, comparator_2_eq, WrReg, not_1_out);
  and and_2 (and_2_out, comparator_1_eq, WrReg, not_2_out);
  Comparator #(.width(5), .mode("unsigned")) comparator_3 (
    .a(WrAddr), .b({5{1'b0}}), .eq(comparator_3_eq));  // open: gt, lt
  not not_1 (not_1_out, comparator_3_eq);
  Comparator #(.width(5), .mode("unsigned")) comparator_4 (
    .a(WrAddr), .b({5{1'b0}}), .eq(comparator_4_eq));  // open: gt, lt
  not not_2 (not_2_out, comparator_4_eq);
endmodule

module Overflow_Unit (
  input  Add,
  input  Sub,
  input  ASign,
  input  BSign,
  input  ResultSign,
  output Overflow
);

  wire and_1_out, and_2_out, or_1_out, xnor_1_out, xor_1_out, xor_2_out;

  xnor xnor_1 (xnor_1_out, ASign, BSign);
  xor xor_1 (xor_1_out, ASign, BSign);
  and and_1 (and_1_out, xnor_1_out, Add);
  and and_2 (and_2_out, xor_1_out, Sub);
  or or_1 (or_1_out, and_1_out, and_2_out);
  xor xor_2 (xor_2_out, ResultSign, ASign);
  and and_3 (Overflow, or_1_out, xor_2_out);

  // Notes on the sheet:
  //   Overflow occurs when doing addition and sign(A) == sign(B) && sign(result) != sign(A)
  //   Or
  //   Overflow occurs when doing subtraction and sign(A) != sign(B) && sign(result) != sign(A)
endmodule

module ALU_Control_Unit (
  output [2:0] ALUOp,
  output [3:0] ALUCtl,
  output [5:0] func
);

  ROM #(.addrWidth(9), .dataWidth(4)) rom_1 (.addr({func, ALUOp}), .data(ALUCtl));  // open: sel

  // Notes on the sheet:
  //   contents of rom_1 (hex, n*v repeats v):
  //   64*7 64*5 9 0 8 29*0 7 0 5 0 3 6 0 4 0 0 2 1 20*0 64*7 64*3 64*6 64*2
endmodule

module Main_Control_Unit (
  output [1:0] out_1,
  output out_2,
  output [1:0] out_3,
  output out_4,
  output [5:0] op,
  output out_6,
  output out_7,
  output out_8,
  output [2:0] out_9
);

  ROM #(.addrWidth(6), .dataWidth(12)) rom_1 (
    .addr(op), .data({out_9, out_8, out_7, out_6, out_4, out_3, out_2, out_1}));  // open: sel

  // Notes on the sheet:
  //   contents of rom_1 (hex, n*v repeats v):
  //   442 0 0 0 9 0 0 0 243 0 246 0 244 245 21*0 2e0 7*0 210
endmodule
